# Fritzing sketch Wiring (saved by Fritzing 0.9.9b)

parts:
  MCU1 = Raspberry Pi Zero
  S1 = Reed switch [package=THT]
  LED1 = LED - 3mm [color="Red (633nm)" current=0.030 package="3 mm [THT]"]
  R1 = Resistor [tolerance=±5% power=0.25 resistance=220 package=THT]
  R2 = Resistor [tolerance=±5% power=0.25 resistance=10k package=THT]
  Power_plug1 = Power plug

nets:
  N1: MCU1.pin_1, R2.Pin_0
  N2: MCU1.pin_4, Power_plug1.VCC
  N3: MCU1.pin_6, MCU1.pin_14, MCU1.pin_39, LED1.cathode, Power_plug1.GND
  N4: MCU1.pin_38, S1.pin_2
  N5: MCU1.pin_40, R1.Pin_0
  N6: S1.pin_1, R2.Pin_1
  N7: LED1.anode, R1.Pin_1
